# Fritzing sketch IOTSKETCHFRITZING (saved by Fritzing 0.9.3b)

parts:
  U1 = ESP8266 NodeMCU LoLin module
  LED2 = LED - 5mm [color="Red (633nm)" package="5 mm [THT]"]
  J1 = Basic Servo
  Part1 = RFID-RC522-v2

nets:
  N1: U1.D0, J1.pulse
  N2: U1.D1, LED2.anode
  N3: U1.D3, Part1.RST
  N4: U1.D4, Part1.SDA
  3V3: U1.3V3, J1.vcc, Part1.3.3V
  GND: U1.GND, LED2.cathode, J1.gnd, Part1.GND
  N5: U1.D6, Part1.MISO
  N6: U1.D7, Part1.MOSI

custom parts:
  ESP8266 NodeMCU LoLin module: ESP8266 based NodeMCU
  RFID-RC522-v2: A simple China made RFID-RC522 Reader; do check the pin labels, as this is a MFRC522 based clone.
